# Fritzing sketch eindopdracht (saved by Fritzing 0.9.3b)
breadboards: 2

parts:
  Part1 = Arduino Nano (Rev3.0) (ICSP)
  DHT1 = DHT11 Humitidy and Temperature Sensor
  Disp1 = LBT2088AH [part_number=LBT2088AH]
  IC1 = SHIFT REGISTER [package=dil16]
  IC2 = SHIFT REGISTER [package=dil16]
  R1 = Resistor [tolerance=±5% resistance=220 package=THT]
  R2 = Resistor [tolerance=±5% resistance=220 package=THT]
  R3 = Resistor [tolerance=±5% resistance=220 package=THT]
  R4 = Resistor [tolerance=±5% resistance=220 package=THT]
  R5 = Resistor [tolerance=±5% resistance=220 package=THT]
  R6 = Resistor [tolerance=±5% resistance=220 package=THT]
  R7 = Resistor [tolerance=±5% resistance=220 package=THT]
  R8 = Resistor [tolerance=±5% resistance=220 package=THT]

nets:
  GND: Part1.GND, DHT1.GND, IC1.GND, IC1.G, IC2.GND, IC2.G
  N1: Part1.D6, DHT1.DATA
  VCC: Part1.5V, IC1.SCL, IC1.VCC, IC2.SCL, IC2.VCC
  N2: Part1.A2, IC1.SCK, IC2.SCK
  N3: Part1.A1, IC1.RCK, IC2.RCK
  N4: Part1.A0, IC1.SER
  3V3: Part1.3V3, DHT1.VDD
  N5: Disp1.pin_9, R6.Pin_1
  N6: Disp1.pin_10, IC2.QD
  N7: Disp1.pin_11, IC2.QF
  N8: Disp1.pin_12, R7.Pin_1
  N9: Disp1.pin_13, IC2.QA
  N10: Disp1.pin_14, R8.Pin_1
  N11: Disp1.pin_15, IC2.QG
  N12: Disp1.pin_16, IC2.QH
  N13: IC1.QB, R8.Pin_0
  N14: IC1.QC, R5.Pin_1
  N15: IC1.QD, R7.Pin_0
  N16: IC1.QE, R1.Pin_1
  N17: IC1.QF, R4.Pin_1
  N18: IC1.QG, R2.Pin_1
  N19: IC1.QH, R3.Pin_1
  N20: IC1.QH*, IC2.SER
  N21: IC1.QA, R6.Pin_0

custom parts:
  DHT11 Humitidy and Temperature Sensor: DHT11 Humidity and Temperature Sensor
