# Fritzing sketch opdracht2_1_fritzing (saved by Fritzing 0.9.3b)
breadboards: 1

parts:
  Part1 = Arduino Nano (Rev3.0) (ICSP)
  R1 = Resistor [tolerance=±5% resistance=220 package=THT]
  DI1 = 7-Segment LED Display [package=THT]
  DI2 = 7-Segment LED Display [package=THT]  # not connected

nets:
  N1: Part1.D2, DI1.commAnode#7
  N2: Part1.D3, DI1.cathodeA
  N3: Part1.D4, DI1.cathodeC
  N4: Part1.D5, DI1.cathodeD
  N5: Part1.5V, R1.Pin_0, R1.Pin_1, DI1.cathodeG
  N6: Part1.A2, DI1.commAnode#2
  N7: Part1.A1, DI1.cathodeF
  N8: Part1.A0, DI1.cathodeE
