# Fritzing sketch opdracht2_2_fritzing (saved by Fritzing 0.9.3b)
breadboards: 1

parts:
  Part1 = Arduino Nano (Rev3.0) (ICSP)
  R1 = Resistor [tolerance=±5% resistance=220 package=THT]
  DI1 = 7-Segment LED Display [package=THT]
  DI2 = 7-Segment LED Display [package=THT]

nets:
  N1: Part1.D2, DI1.commAnode#7
  N2: Part1.D3, DI1.cathodeA
  N3: Part1.D4, DI1.cathodeC
  N4: Part1.D5, DI1.cathodeD
  N5: Part1.D8, DI2.commAnode#7
  N6: Part1.D9, DI2.cathodeA
  N7: Part1.D10, DI2.commAnode#2
  N8: Part1.D11/MOSI, DI2.cathodeD
  N9: Part1.5V, R1.Pin_0, R1.Pin_1, DI1.cathodeG, DI2.cathodeB
  N10: Part1.A6, DI2.cathodeF
  N11: Part1.A5, DI2.cathodeG
  N12: Part1.A4, DI2.cathodeE
  N13: Part1.A2, DI1.commAnode#2
  N14: Part1.A1, DI1.cathodeF
  N15: Part1.A0, DI1.cathodeE
