# Fritzing sketch opdracht3_1_fritzing (saved by Fritzing 0.9.3b)
breadboards: 1

parts:
  Part1 = Arduino Nano (Rev3.0) (ICSP)
  LED1 = LED - 5mm [color="Red (633nm)" package="5 mm [THT]"]
  R1 = Resistor [tolerance=±5% resistance=220 package=THT]
  R3 = Resistor [tolerance=±5% resistance=220 package=THT]
  R4 = Resistor [tolerance=±5% resistance=220 package=THT]
  R5 = Resistor [tolerance=±5% resistance=220 package=THT]
  R6 = Resistor [tolerance=±5% resistance=220 package=THT]
  R7 = Resistor [tolerance=±5% resistance=220 package=THT]
  R8 = Resistor [tolerance=±5% resistance=220 package=THT]
  LED2 = LED - 5mm [color="Red (633nm)" package="5 mm [THT]"]
  LED3 = LED - 5mm [color="Red (633nm)" package="5 mm [THT]"]
  LED4 = LED - 5mm [color="Red (633nm)" package="5 mm [THT]"]
  LED5 = LED - 5mm [color="Red (633nm)" package="5 mm [THT]"]
  LED6 = LED - 5mm [color="Red (633nm)" package="5 mm [THT]"]
  LED7 = LED - 5mm [color="Red (633nm)" package="5 mm [THT]"]
  S1 = Momentary Switch [package=ksa_sealed_tac_switch]

nets:
  N1: Part1.GND, R1.Pin_0, R3.Pin_0, R4.Pin_0, R5.Pin_0, R6.Pin_1, R7.Pin_1, R8.Pin_1, S1.1
  N2: Part1.D2, S1.3
  N3: Part1.D3, LED1.anode
  N4: Part1.D4, LED2.anode
  N5: Part1.D5, LED3.anode
  N6: Part1.D6, LED4.anode
  N7: Part1.D7, LED5.anode
  N8: Part1.D8, LED6.anode
  N9: Part1.D9, LED7.anode
  N10: LED1.cathode, R5.Pin_1
  N11: R1.Pin_1, LED3.cathode
  N12: R3.Pin_1, LED2.cathode
  N13: R4.Pin_1, LED4.cathode
  N14: R6.Pin_0, LED5.cathode
  N15: R7.Pin_0, LED6.cathode
  N16: R8.Pin_0, LED7.cathode
