# Fritzing sketch opdracht3_2_fritzing (saved by Fritzing 0.9.3b)
breadboards: 1

parts:
  Part1 = Arduino Nano (Rev3.0) (ICSP)
  R1 = Rotary Potentiometer (Small) [maximum_resistance=100kΩ package=THT]
  SP1 = SPEAKER [package=pcb_mount_speaker]

nets:
  N1: Part1.GND, R1.leg1, SP1.+
  N2: Part1.5V, R1.leg2
  N3: Part1.A0, R1.wiper
  N4: Part1.D13/SCK, SP1.-
