# Fritzing sketch opdracht4_2_fritzing (saved by Fritzing 0.9.3b)
breadboards: 1

parts:
  Part1 = Arduino Nano (Rev3.0) (ICSP)
  R1 = Resistor [tolerance=±5% resistance=220 package=THT]
  LED1 = smd LED [color="Red (633nm)" package="1206 [SMD]"]

nets:
  N1: Part1.GND, LED1.cathode
  N2: Part1.D13/SCK, R1.Pin_1
  N3: R1.Pin_0, LED1.anode
