# Fritzing sketch opdracht5_2_fritzing (saved by Fritzing 0.9.3b)
breadboards: 1

parts:
  Part1 = Arduino Nano (Rev3.0) (ICSP)
  LCD1 = LCD screen
  R1 = Rotary Potentiometer (Small) [maximum_resistance=100kΩ package=THT]

nets:
  GND: Part1.GND, LCD1.VSS, LCD1.R/W, R1.leg2
  5V: Part1.5V, LCD1.VDD, R1.leg1
  N1: Part1.A5, LCD1.E
  N2: Part1.A4, LCD1.RS
  N3: Part1.A3, LCD1.DB7
  N4: Part1.A2, LCD1.DB6
  N5: Part1.A1, LCD1.DB5
  N6: Part1.A0, LCD1.DB4
  N7: LCD1.V0, R1.wiper
